# Fritzing sketch LED and Photoresistor Circuit (saved by Fritzing 0.9.3b)
breadboards: 1

parts:
  U1 = NodeMCU V1.0
  R1 = Resistor [tolerance=±5% resistance=10k package=THT]
  R2 = Photocell (LDR) [package=THT]
  LED1 = LED - 5mm [color="Red (633nm)" package="5 mm [THT]"]

nets:
  N1: U1.3V3, R2.pin_1
  N2: U1.GND, R1.Pin_1, LED1.cathode
  N3: U1.D7, LED1.anode
  N4: U1.A0, R1.Pin_0, R2.pin_0

custom parts:
  NodeMCU V1.0: ESP8266 based NodeMCU
